# Fritzing sketch sketch (saved by Fritzing 0.9.3b)
breadboards: 1

parts:
  Part1 = Arduino Uno (Rev3)
  R1 = Resistor [tolerance=±5% resistance=330 package=THT]
  R2 = Resistor [tolerance=±5% resistance=330 package=THT]
  R3 = Resistor [tolerance=±5% resistance=330 package=THT]
  R4 = Resistor [tolerance=±5% resistance=330 package=THT]
  LED1 = LED - 5mm [color="Green (570nm)" package="5 mm [THT]"]
  LED2 = LED - 5mm [color="Yellow (595nm)" package="5 mm [THT]"]
  LED3 = LED - 5mm [color="Yellow (595nm)" package="5 mm [THT]"]
  LED4 = LED - 5mm [color="Yellow (595nm)" package="5 mm [THT]"]
  Part2 = Breakout Board for Electret Microphone

nets:
  N1: Part1.A0, Part2.AUD
  N2: Part1.D11_PWM/MOSI, LED1.anode
  N3: Part1.D2, LED4.anode
  N4: Part1.D4, LED3.anode
  N5: Part1.D7, LED2.anode
  N6: Part1.GND, R1.Pin_1, R2.Pin_1, R3.Pin_1, R4.Pin_1
  N7: R1.Pin_0, LED4.cathode
  N8: R2.Pin_0, LED3.cathode
  N9: R3.Pin_0, LED2.cathode
  N10: R4.Pin_0, LED1.cathode

notes:
  The microphone part it's not the same used.
